# Fritzing sketch Transistor (saved by Fritzing 0.9.1b)
breadboards: 1

parts:
  Q1 = NPN-Transistor [package="TO92 [THT]"]
  R1 = Resistor [tolerance=±5% resistance=220 package=THT]
  R3 = Resistor [tolerance=±5% resistance=100 package=THT]
  C1 = Ceramic Capacitor [capacitance=100nF package="100 mil [THT, multilayer]"]
  L1 = Inductor [inductance=20 package="400 mil [THT]"]
  R2 = Resistor [tolerance=±5% resistance=400 package=THT]

nets:
  N1: Q1.E, R2.Pin_0
  N2: Q1.B, R1.Pin_1
  N3: Q1.C, C1.0, L1.pin_0
  N4: R1.Pin_0, R3.Pin_0, R2.Pin_1
  N5: R3.Pin_1, C1.1, L1.pin_1
